# Fritzing sketch shoutbox-attiny85 (saved by Fritzing 0.9.3b)
breadboards: 1

parts:
  U1 = attiny85 [package=dip]
  S1 = Pushbutton [package="[THT]"]
  R1 = PHOTOCELL [package=photocell]
  R2 = Resistor [tolerance=±5% resistance=10k package="2512 [SMD]"]
  Part2 = SparkFun Load Sensor Combinator
  R3 = Resistor [tolerance=±5% resistance=10k package="2512 [SMD]"]
  SP1 = SPEAKER [package=pcb_mount_speaker]
  LED1 = smd LED [color="Blue (430nm)" package="0805 [SMD]"]
  R4 = Resistor [tolerance=±5% resistance=10k package="2512 [SMD]"]
  VCC2 = 4 x AAA Battery Mount

nets:
  N1: U1.Pin_2, S1.Pin_1, S1.Pin_2, R3.Pin_0
  N2: U1.Pin_3, Part2.E-
  N3: U1.Pin_4, R2.Pin_1, R3.Pin_1, R4.Pin_1, VCC2.-
  N4: U1.Pin_5, LED1.cathode
  N5: U1.Pin_6, Part2.E+
  N6: U1.Pin_7, R1.P$2, R2.Pin_0
  N7: U1.Pin_8, S1.Pin_3, S1.Pin_4, R1.P$1, Part2.5, VCC2.+
  N8: Part2.1, SP1.+
  N9: LED1.anode, R4.Pin_0
